// Logisim project calculator.circ as structural Verilog: 9 circuits, main circuit main
module main (
  input  A1,
  input  A0,
  input  B1,
  input  B0,
  input  [1:0] in_5,
  output R1,
  output R0,
  output Q1,
  output Q0
);

  wire add_1_s0, add_1_s1, add_1_s2, add_1_s3, div_1_q0, div_1_q1, div_1_r0, div_1_r1, mul_1_p0, mul_1_p1,
       mul_1_p2, mul_1_p3, sub_1_d0, sub_1_d1, sub_1_d2, sub_1_d3;

  add add_1 (.A1(A1), .A0(A0), .B1(B1), .B0(B0), .S3(add_1_s3), .S2(add_1_s2), .S1(add_1_s1), .S0(add_1_s0));
  sub sub_1 (.A1(A1), .A0(A0), .B1(B1), .B0(B0), .D3(sub_1_d3), .D2(sub_1_d2), .D1(sub_1_d1), .D0(sub_1_d0));
  mul mul_1 (.A1(A1), .A0(A0), .B1(B1), .B0(B0), .P3(mul_1_p3), .P2(mul_1_p2), .P1(mul_1_p1), .P0(mul_1_p0));
  div div_1 (.A1(A1), .A0(A0), .B1(B1), .B0(B0), .R1(div_1_r1), .Q1(div_1_q1), .R0(div_1_r0), .Q0(div_1_q0));
  Multiplexer #(.select(2)) multiplexer_1 (
    .in0(add_1_s3), .in1(sub_1_d3), .in2(mul_1_p3), .in3(div_1_r1), .out(R1), .sel(in_5));  // open: en
  Multiplexer #(.select(2)) multiplexer_2 (
    .in0(add_1_s2), .in1(sub_1_d2), .in2(mul_1_p2), .in3(div_1_r0), .out(R0), .sel(in_5));  // open: en
  Multiplexer #(.select(2)) multiplexer_3 (
    .in0(add_1_s1), .in1(sub_1_d1), .in2(mul_1_p1), .in3(div_1_q1), .out(Q1), .sel(in_5));  // open: en
  Multiplexer #(.select(2)) multiplexer_4 (
    .in0(add_1_s0), .in1(sub_1_d0), .in2(mul_1_p0), .in3(div_1_q0), .out(Q0), .sel(in_5));  // open: en
endmodule

// ÷
module div (
  input  A1,
  input  A0,
  input  B1,
  input  B0,
  output Q1,
  output Q0,
  output R1,
  output R0
);

  wire and_2_out, and_3_out, and_4_out, and_5_out, and_6_out, not_1_out, not_2_out, not_3_out, not_4_out,
       not_5_out, not_6_out;

  and and_1 (Q1, A1, not_1_out, B0);
  not not_1 (not_1_out, B1);
  and and_2 (and_2_out, A0, not_2_out, B0);
  not not_2 (not_2_out, B1);
  and and_3 (and_3_out, A1, B1, not_3_out);
  not not_3 (not_3_out, B0);
  and and_4 (and_4_out, A1, A0, B1);
  not not_4 (not_4_out, A0);
  not not_5 (not_5_out, A1);
  and and_5 (and_5_out, not_5_out, A0, B1);
  and and_6 (and_6_out, A0, B1, not_6_out);
  not not_6 (not_6_out, B0);
  or or_1 (Q0, and_2_out, and_3_out, and_4_out);
  and and_7 (R1, A1, not_4_out, B1, B0);
  or or_2 (R0, and_5_out, and_6_out);
endmodule

// x
module mul (
  input  A1,
  input  A0,
  input  B1,
  input  B0,
  output P3,
  output P2,
  output P1,
  output P0
);

  wire and_2_out, and_3_out, and_4_out, and_5_out, and_6_out, and_7_out, not_1_out, not_2_out, not_3_out,
       not_4_out, not_5_out, not_6_out;

  and and_1 (P3, A1, A0, B1, B0);
  not not_1 (not_1_out, A0);
  and and_2 (and_2_out, A1, not_1_out, B1);
  and and_3 (and_3_out, A1, B1, not_2_out);
  not not_2 (not_2_out, B0);
  not not_3 (not_3_out, A1);
  and and_4 (and_4_out, not_3_out, A0, B1);
  and and_5 (and_5_out, A0, B1, not_4_out);
  not not_4 (not_4_out, B0);
  and and_6 (and_6_out, A1, not_5_out, B0);
  not not_5 (not_5_out, A0);
  and and_7 (and_7_out, A1, not_6_out, B0);
  not not_6 (not_6_out, B1);
  and and_8 (P0, A0, B0);
  or or_1 (P2, and_2_out, and_3_out);
  or or_2 (P1, and_4_out, and_5_out, and_6_out, and_7_out);
endmodule

// +
module add (
  input  A1,
  input  A0,
  input  B1,
  input  B0,
  output S3,
  output S2,
  output S1,
  output S0
);

  wire and_1_out, and_2_out, and_3_out, and_4_out, and_5_out, and_6_out, and_7_out, and_8_out, and_9_out,
       and_10_out, and_11_out, not_1_out, not_2_out, not_3_out, not_4_out, not_5_out, not_6_out, not_7_out,
       not_8_out, not_9_out, not_10_out, not_11_out, not_12_out;

  and and_1 (and_1_out, A0, B1, B0);
  and and_2 (and_2_out, A1, B1);
  and and_3 (and_3_out, A1, A0, B0);
  not not_1 (not_1_out, A1);
  not not_2 (not_2_out, A0);
  not not_3 (not_3_out, A1);
  not not_4 (not_4_out, B0);
  not not_5 (not_5_out, A1);
  not not_6 (not_6_out, B1);
  not not_7 (not_7_out, A0);
  not not_8 (not_8_out, B1);
  not not_9 (not_9_out, B1);
  not not_10 (not_10_out, B0);
  not not_11 (not_11_out, A0);
  and and_4 (and_4_out, not_11_out, B0);
  and and_5 (and_5_out, A0, not_12_out);
  not not_12 (not_12_out, B0);
  or or_1 (S2, and_1_out, and_2_out, and_3_out);
  and and_6 (and_6_out, not_1_out, not_2_out, B1);
  and and_7 (and_7_out, not_3_out, B1, not_4_out);
  and and_8 (and_8_out, not_5_out, A0, not_6_out, B0);
  and and_9 (and_9_out, A1, not_7_out, not_8_out);
  and and_10 (and_10_out, A1, not_9_out, not_10_out);
  and and_11 (and_11_out, A1, A0, B1, B0);
  or or_2 (S0, and_4_out, and_5_out);
  or or_3 (S1, and_6_out, and_7_out, and_8_out, and_9_out, and_10_out, and_11_out);

  assign S3 = 1'b0;
endmodule

// -
module sub (
  input  A1,
  input  A0,
  input  B1,
  input  B0,
  output D3,
  output D2,
  output D1,
  output D0
);

  wire and_1_out, and_2_out, and_3_out, and_4_out, and_5_out, and_6_out, and_7_out, and_8_out, and_9_out,
       and_10_out, and_11_out, and_12_out, and_13_out, and_14_out, not_1_out, not_2_out, not_3_out,
       not_4_out, not_5_out, not_6_out, not_7_out, not_8_out, not_9_out, not_10_out, not_11_out, not_12_out,
       not_13_out, not_14_out, not_15_out, not_16_out, not_17_out, not_18_out, not_19_out, not_20_out;

  not not_1 (not_1_out, A1);
  not not_2 (not_2_out, A0);
  and and_1 (and_1_out, not_1_out, not_2_out, B0);
  not not_3 (not_3_out, A1);
  and and_2 (and_2_out, not_3_out, B1);
  not not_4 (not_4_out, A0);
  and and_3 (and_3_out, not_4_out, B1, B0);
  not not_5 (not_5_out, A1);
  not not_6 (not_6_out, A0);
  and and_4 (and_4_out, not_5_out, not_6_out, B0);
  not not_7 (not_7_out, A1);
  and and_5 (and_5_out, not_7_out, B1);
  not not_8 (not_8_out, A0);
  and and_6 (and_6_out, not_8_out, B1, B0);
  not not_9 (not_9_out, A1);
  not not_10 (not_10_out, A0);
  not not_11 (not_11_out, B1);
  not not_12 (not_12_out, A1);
  not not_13 (not_13_out, B0);
  not not_14 (not_14_out, A1);
  not not_15 (not_15_out, B1);
  not not_16 (not_16_out, B0);
  not not_17 (not_17_out, A0);
  not not_18 (not_18_out, B1);
  not not_19 (not_19_out, A0);
  and and_7 (and_7_out, not_19_out, B0);
  and and_8 (and_8_out, A0, not_20_out);
  not not_20 (not_20_out, B0);
  or or_1 (D3, and_1_out, and_2_out, and_3_out);
  or or_2 (D2, and_4_out, and_5_out, and_6_out);
  and and_9 (and_9_out, not_9_out, not_10_out, not_11_out, B0);
  and and_10 (and_10_out, not_12_out, B1, not_13_out);
  and and_11 (and_11_out, not_14_out, A0, B1);
  and and_12 (and_12_out, A1, not_15_out, not_16_out);
  and and_13 (and_13_out, A1, not_17_out, B1, B0);
  and and_14 (and_14_out, A1, A0, not_18_out);
  or or_3 (D0, and_7_out, and_8_out);
  or or_4 (D1, and_9_out, and_10_out, and_11_out, and_12_out, and_13_out, and_14_out);
endmodule

module div_nand (
  input  A1,
  input  A0,
  input  B1,
  input  B0,
  output Q1,
  output Q0,
  output R1,
  output R0
);

  wire nand_1_out, nand_2_out, nand_3_out, nand_4_out, nand_5_out, nand_6_out, nand_7_out, nand_8_out,
       nand_9_out, nand_10_out, nand_11_out, nand_12_out, nand_13_out;

  nand nand_1 (nand_1_out, B1, B1);
  nand nand_2 (nand_2_out, B1, B1);
  nand nand_3 (nand_3_out, B0, B0);
  nand nand_4 (nand_4_out, A0, A0);
  nand nand_5 (nand_5_out, A1, A1);
  nand nand_6 (nand_6_out, B0, B0);
  nand nand_7 (nand_7_out, A1, nand_1_out, B0);
  nand nand_8 (nand_8_out, A0, nand_2_out, B0);
  nand nand_9 (nand_9_out, A1, B1, nand_3_out);
  nand nand_10 (nand_10_out, A1, A0, B1);
  nand nand_11 (nand_11_out, A1, nand_4_out, B1, B0);
  nand nand_12 (nand_12_out, nand_5_out, A0, B1);
  nand nand_13 (nand_13_out, A0, B1, nand_6_out);
  nand nand_14 (Q1, nand_7_out, nand_7_out);
  nand nand_15 (Q0, nand_8_out, nand_9_out, nand_10_out);
  nand nand_16 (R1, nand_11_out, nand_11_out);
  nand nand_17 (R0, nand_12_out, nand_13_out);
endmodule

module mul_nand (
  input  A1,
  input  A0,
  input  B1,
  input  B0,
  output P3,
  output P2,
  output P1,
  output P0
);

  wire nand_1_out, nand_2_out, nand_3_out, nand_4_out, nand_5_out, nand_6_out, nand_7_out, nand_8_out,
       nand_10_out, nand_11_out, nand_12_out, nand_13_out, nand_14_out, nand_15_out;

  nand nand_1 (nand_1_out, A1, A0, B1, B0);
  nand nand_2 (nand_2_out, A0, A0);
  nand nand_3 (nand_3_out, B0, B0);
  nand nand_4 (nand_4_out, A1, A1);
  nand nand_5 (nand_5_out, B0, B0);
  nand nand_6 (nand_6_out, A0, A0);
  nand nand_7 (nand_7_out, B1, B1);
  nand nand_8 (nand_8_out, A0, B0);
  nand nand_9 (P3, nand_1_out, nand_1_out);
  nand nand_10 (nand_10_out, A1, nand_2_out, B1);
  nand nand_11 (nand_11_out, A1, B1, nand_3_out);
  nand nand_12 (nand_12_out, nand_4_out, A0, B1);
  nand nand_13 (nand_13_out, A0, B1, nand_5_out);
  nand nand_14 (nand_14_out, A1, nand_6_out, B0);
  nand nand_15 (nand_15_out, A1, nand_7_out, B0);
  nand nand_16 (P0, nand_8_out, nand_8_out);
  nand nand_17 (P2, nand_10_out, nand_11_out);
  nand nand_18 (P1, nand_12_out, nand_13_out, nand_14_out, nand_15_out);
endmodule

module add_nand (
  input  A1,
  input  A0,
  input  B1,
  input  B0,
  output S3,
  output S2,
  output S1,
  output S0
);

  wire nand_1_out, nand_2_out, nand_3_out, nand_4_out, nand_5_out, nand_6_out, nand_7_out, nand_8_out,
       nand_9_out, nand_10_out, nand_11_out, nand_12_out, nand_13_out, nand_14_out, nand_15_out, nand_17_out,
       nand_18_out, nand_19_out, nand_20_out, nand_21_out, nand_22_out, nand_23_out, nand_24_out;

  nand nand_1 (nand_1_out, A0, B1, B0);
  nand nand_2 (nand_2_out, A1, B1);
  nand nand_3 (nand_3_out, A1, A0, B0);
  nand nand_4 (nand_4_out, A1, A1);
  nand nand_5 (nand_5_out, A0, A0);
  nand nand_6 (nand_6_out, A1, A1);
  nand nand_7 (nand_7_out, B0, B0);
  nand nand_8 (nand_8_out, A1, A1);
  nand nand_9 (nand_9_out, B1, B1);
  nand nand_10 (nand_10_out, A0, A0);
  nand nand_11 (nand_11_out, B1, B1);
  nand nand_12 (nand_12_out, B1, B1);
  nand nand_13 (nand_13_out, B0, B0);
  nand nand_14 (nand_14_out, A0, A0);
  nand nand_15 (nand_15_out, B0, B0);
  nand nand_16 (S2, nand_1_out, nand_2_out, nand_3_out);
  nand nand_17 (nand_17_out, nand_4_out, nand_5_out, B1);
  nand nand_18 (nand_18_out, nand_6_out, B1, nand_7_out);
  nand nand_19 (nand_19_out, nand_8_out, A0, nand_9_out, B0);
  nand nand_20 (nand_20_out, A1, nand_10_out, nand_11_out);
  nand nand_21 (nand_21_out, A1, nand_12_out, nand_13_out);
  nand nand_22 (nand_22_out, A1, A0, B1, B0);
  nand nand_23 (nand_23_out, nand_14_out, B0);
  nand nand_24 (nand_24_out, A0, nand_15_out);
  nand nand_25 (S1, nand_17_out, nand_18_out, nand_19_out, nand_20_out, nand_21_out, nand_22_out);
  nand nand_26 (S0, nand_23_out, nand_24_out);

  assign S3 = 1'b0;
endmodule

module sub_nand (
  input  A1,
  input  A0,
  input  B1,
  input  B0,
  output D3,
  output D2,
  output D1,
  output D0
);

  wire nand_1_out, nand_2_out, nand_3_out, nand_4_out, nand_5_out, nand_6_out, nand_7_out, nand_8_out,
       nand_9_out, nand_10_out, nand_11_out, nand_12_out, nand_13_out, nand_14_out, nand_15_out, nand_16_out,
       nand_17_out, nand_18_out, nand_19_out, nand_20_out, nand_21_out, nand_22_out, nand_23_out,
       nand_24_out, nand_25_out, nand_26_out, nand_27_out, nand_28_out, nand_29_out, nand_30_out,
       nand_31_out, nand_32_out, nand_33_out, nand_34_out;

  nand nand_1 (nand_1_out, A1, A1);
  nand nand_2 (nand_2_out, A0, A0);
  nand nand_3 (nand_3_out, A1, A1);
  nand nand_4 (nand_4_out, A0, A0);
  nand nand_5 (nand_5_out, A1, A1);
  nand nand_6 (nand_6_out, A0, A0);
  nand nand_7 (nand_7_out, A1, A1);
  nand nand_8 (nand_8_out, A0, A0);
  nand nand_9 (nand_9_out, A1, A1);
  nand nand_10 (nand_10_out, A0, A0);
  nand nand_11 (nand_11_out, B1, B1);
  nand nand_12 (nand_12_out, A1, A1);
  nand nand_13 (nand_13_out, B0, B0);
  nand nand_14 (nand_14_out, A1, A1);
  nand nand_15 (nand_15_out, B1, B1);
  nand nand_16 (nand_16_out, B0, B0);
  nand nand_17 (nand_17_out, A0, A0);
  nand nand_18 (nand_18_out, B1, B1);
  nand nand_19 (nand_19_out, A0, A0);
  nand nand_20 (nand_20_out, B0, B0);
  nand nand_21 (nand_21_out, nand_1_out, nand_2_out, B0);
  nand nand_22 (nand_22_out, nand_3_out, B1);
  nand nand_23 (nand_23_out, nand_4_out, B1, B0);
  nand nand_24 (nand_24_out, nand_5_out, nand_6_out, B0);
  nand nand_25 (nand_25_out, nand_7_out, B1);
  nand nand_26 (nand_26_out, nand_8_out, B1, B0);
  nand nand_27 (nand_27_out, nand_9_out, nand_10_out, nand_11_out, B0);
  nand nand_28 (nand_28_out, nand_12_out, B1, nand_13_out);
  nand nand_29 (nand_29_out, nand_14_out, A0, B1);
  nand nand_30 (nand_30_out, A1, nand_15_out, nand_16_out);
  nand nand_31 (nand_31_out, A1, nand_17_out, B1, B0);
  nand nand_32 (nand_32_out, A1, A0, nand_18_out);
  nand nand_33 (nand_33_out, nand_19_out, B0);
  nand nand_34 (nand_34_out, A0, nand_20_out);
  nand nand_35 (D3, nand_21_out, nand_22_out, nand_23_out);
  nand nand_36 (D2, nand_24_out, nand_25_out, nand_26_out);
  nand nand_37 (D1, nand_27_out, nand_28_out, nand_29_out, nand_30_out, nand_31_out, nand_32_out);
  nand nand_38 (D0, nand_33_out, nand_34_out);
endmodule
