// Logisim project lol.circ as structural Verilog
module _2_scomp (
  input  a3,
  input  a2,
  input  a1,
  input  a0,
  output y3,
  output y2,
  output y1,
  output y0
);

  wire and_1_out, and_2_out, and_3_out, and_4_out, and_5_out, and_6_out, and_7_out, and_8_out, and_9_out,
       not_1_out, not_2_out, not_3_out, not_4_out, not_5_out, not_6_out, not_7_out, not_8_out, not_9_out,
       not_10_out, not_11_out;

  not not_1 (not_1_out, a3);
  and and_1 (and_1_out, not_1_out, a0);
  not not_2 (not_2_out, a3);
  and and_2 (and_2_out, not_2_out, a1);
  not not_3 (not_3_out, a3);
  and and_3 (and_3_out, not_3_out, a2);
  and and_4 (and_4_out, a3, not_4_out, not_5_out);
  not not_4 (not_4_out, a2);
  not not_5 (not_5_out, a0);
  not not_6 (not_6_out, a2);
  and and_5 (and_5_out, not_6_out, a0);
  not not_7 (not_7_out, a2);
  and and_6 (and_6_out, not_7_out, a1);
  and and_7 (and_7_out, a2, not_8_out, not_9_out);
  not not_8 (not_8_out, a1);
  not not_9 (not_9_out, a0);
  not not_10 (not_10_out, a1);
  and and_8 (and_8_out, not_10_out, a0);
  and and_9 (and_9_out, a1, not_11_out);
  not not_11 (not_11_out, a0);
  or or_1 (y3, and_1_out, and_2_out, and_3_out, and_4_out);
  or or_2 (y2, and_5_out, and_6_out, and_7_out);
  or or_3 (y1, and_8_out, and_9_out);

  assign y0 = a0;
endmodule

module _1 (
  input  a3,
  input  a2,
  input  a1,
  input  a0,
  output y3,
  output y2,
  output y1,
  output y0
);

  wire and_1_out, and_2_out, and_3_out, and_4_out, and_5_out, and_6_out, and_7_out, and_8_out, and_9_out,
       and_10_out, and_11_out, not_1_out, not_2_out, not_3_out, not_4_out, not_5_out, not_6_out, not_7_out,
       not_8_out, not_9_out, not_10_out, not_11_out, or_1_out, or_3_out, or_4_out;

  not not_1 (not_1_out, a3);
  not not_2 (not_2_out, a3);
  not not_3 (not_3_out, a3);
  and and_1 (and_1_out, a3, not_4_out);
  not not_4 (not_4_out, a2);
  not not_5 (not_5_out, a0);
  not not_6 (not_6_out, a2);
  and and_2 (and_2_out, not_6_out, a0);
  not not_7 (not_7_out, a2);
  and and_3 (and_3_out, not_7_out, a1);
  and and_4 (and_4_out, a2, not_8_out);
  not not_8 (not_8_out, a1);
  not not_9 (not_9_out, a0);
  not not_10 (not_10_out, a1);
  and and_5 (and_5_out, not_10_out, a0);
  and and_6 (and_6_out, a1, not_11_out);
  not not_11 (not_11_out, a0);
  and and_7 (and_7_out, not_1_out, a0);
  and and_8 (and_8_out, not_2_out, a1);
  and and_9 (and_9_out, not_3_out, a2);
  and and_10 (and_10_out, and_1_out, not_5_out);
  or or_1 (or_1_out, and_2_out, and_3_out);
  and and_11 (and_11_out, and_4_out, not_9_out);
  or or_2 (y1, and_5_out, and_6_out);
  or or_3 (or_3_out, and_7_out, and_8_out);
  or or_4 (or_4_out, and_9_out, and_10_out);
  or or_5 (y2, or_1_out, and_11_out);
  or or_6 (y3, or_3_out, or_4_out);

  assign y0 = a0;
endmodule

module _22 (
  input  A0,
  input  A1,
  input  A2,
  input  A3,
  output Y3,
  output Y2,
  output Y1,
  output Y0
);

  wire adder_1_cout, adder_2_cout, adder_3_cout, xor_1_out, xor_2_out, xor_3_out, xor_4_out, xor_5_out;

  xor xor_1 (xor_1_out, 1'b1, 1'b1);
  xor xor_2 (xor_2_out, 1'b1, A0);
  xor xor_3 (xor_3_out, 1'b1, A1);
  xor xor_4 (xor_4_out, 1'b1, A2);
  xor xor_5 (xor_5_out, 1'b1, A3);
  Adder #(.width(1)) adder_1 (.a(1'b1), .b(xor_2_out), .out(Y0), .cin(xor_1_out), .cout(adder_1_cout));
  Adder #(.width(1)) adder_2 (.a(xor_1_out), .b(xor_3_out), .out(Y1), .cin(adder_1_cout), .cout(adder_2_cout));
  Adder #(.width(1)) adder_3 (.a(xor_1_out), .b(xor_4_out), .out(Y2), .cin(adder_2_cout), .cout(adder_3_cout));
  Adder #(.width(1)) adder_4 (.a(xor_1_out), .b(xor_5_out), .out(Y3), .cin(adder_3_cout));  // open: cout
endmodule

module _2_s_Comp_XOR (
  input  A0,
  input  A3,
  input  A2,
  input  A1,
  output Y0,
  output Y3,
  output Y2,
  output Y1
);

  wire or_1_out, or_2_out;

  xor xor_1 (Y1, A0, A1);
  or or_1 (or_1_out, A0, A1);
  xor xor_2 (Y2, or_1_out, A2);
  or or_2 (or_2_out, or_1_out, A2);
  xor xor_3 (Y3, or_2_out, A3);

  assign Y0 = A0;
endmodule
